# Fritzing sketch MicroRobotCircuit (saved by Fritzing 1.0.3b)

parts:
  WeMos_D1_Mini1 = WeMos D1 Mini
  Part1 = Motor Driver 1A Dual TB6612FNG
  M1 = DC Motor [voltage_(max)=6V voltage_(min)=3V]
  M2 = DC Motor [voltage_(max)=6V voltage_(min)=3V]
  M3 = RioRand LM2596
  VCC1 = Battery [internal_resistance=0.1Ω]
  M4 = Keyes l9110 Fan module [package=THT]
  S1 = Toggle Switch [package=THT]

nets:
  3V3: WeMos_D1_Mini1.3V3, Part1.VCC
  N1: WeMos_D1_Mini1.5V, Part1.VM, M3.Pin_1, S1.COM
  N2: WeMos_D1_Mini1.D0, M4.pin2
  N3: WeMos_D1_Mini1.D1, Part1.PWMB
  N4: WeMos_D1_Mini1.D2, Part1.PWMA
  N5: WeMos_D1_Mini1.D4, Part1.AIN1
  N6: WeMos_D1_Mini1.D5, Part1.AIN2
  N7: WeMos_D1_Mini1.D6, Part1.BIN2
  N8: WeMos_D1_Mini1.D7, Part1.BIN1
  N9: WeMos_D1_Mini1.G, Part1.GND, M3.Pin_2, VCC1.-
  N10: Part1.B01, M2.pin_2
  N11: Part1.B02, M2.pin_1
  N12: Part1.A02, M1.pin_2
  N13: Part1.A01, M1.pin_1
  N14: M3.Pin_3, M4.pin4
  N15: M3.Pin_4, M4.pin3
  N16: VCC1.+, S1.L2

custom parts:
  Keyes l9110 Fan module: Keyes l9110 Fan module. Done from pictures without an actual board to hand so breadboard may not be fully accurate.
